// Logisim project controller.circ as structural Verilog: 1 circuit, main circuit main
// pla2circ
module main (
  input  S2,
  input  S1,
  input  S0,
  input  TN,
  input  TE,
  input  NIGHT,
  input  WW,
  input  WE,
  output NS2,
  output NS1,
  output NS0
);

  wire U11_out, U12_out, U13_out, U14_out, U15_out, U16_out, U17_out, U18_out, U19_out, U20_out, U21_out,
       U23_out, U24_out, U25_out, U26_out, U27_out, U28_out, U29_out, U30_out, U31_out, U32_out, U34_out,
       U35_out, U36_out, U37_out, U38_out, U39_out, undriven, undriven_2, undriven_3, undriven_4, undriven_5,
       undriven_6, undriven_7, undriven_8, undriven_9, undriven_10, undriven_11, undriven_12, undriven_13,
       undriven_14, undriven_15, undriven_16, undriven_17, undriven_18, undriven_19, undriven_20,
       undriven_21, undriven_22;

  nand U11 (U11_out, undriven, undriven_7, undriven_3);
  not U12 (U12_out, undriven_8);
  not U13 (U13_out, undriven_5);
  not U16 (U16_out, TN);
  not U19 (U19_out, undriven_2);
  not U20 (U20_out, S2);
  nand U24 (U24_out, WW, undriven_19);
  nand U28 (U28_out, undriven_7, undriven_3);
  nand U14 (U14_out, U12_out, undriven_11);
  nand U23 (U23_out, undriven_4, undriven_12);
  nand U27 (U27_out, undriven_20, undriven_9, undriven_11);
  nand U37 (U37_out, TE, undriven_10);
  not U15 (U15_out, U14_out);
  nand U25 (U25_out, U23_out, U24_out);
  nand U29 (U29_out, U28_out, undriven_14);
  not U38 (U38_out, undriven_13);
  nand U17 (U17_out, U15_out, undriven_17, U16_out);
  nand U26 (U26_out, undriven_16, undriven_18);
  nand U30 (U30_out, U29_out, WE, undriven_19);
  nand U36 (U36_out, U25_out, undriven_18, undriven_15);
  nand U39 (U39_out, U37_out, U38_out, undriven_12);
  nand U18 (U18_out, U11_out, U17_out);
  nand U31 (U31_out, U26_out, U27_out, U30_out);
  nand U21 (U21_out, U18_out, undriven_20, U20_out);
  not U32 (U32_out, U31_out);
  not U22 (NS2, U21_out);
  nor U33 (NS1, U32_out, undriven_6);
  not U34 (U34_out, undriven_21);
  nand U35 (U35_out, U34_out, undriven_22);
  nand U40 (NS0, U35_out, U36_out, U39_out);

  // Notes on the sheet:
  //   controller2.txt  by 'pla2circ controller2.txt' (pla2circ v0.21)
endmodule
