// Logisim project traffic light controller.circ as structural Verilog: 8 circuits, main circuit main
module main (
  input  NIGHT
);

  wire button_1_out, button_2_out, C1, C2, or_1_out, or_2_out, or_3_out, or_4_out, TE, TN, U1_rs_e, U1_rs_w,
       U3_wem, U3_wwm, WE, WW;
  wire [1:0] U1_e_green, U1_n_left;
  wire [2:0] U1_w_left;
  wire [3:0] grading_1_out_4;

  Button button_1 (.out(button_1_out));
  Button button_2 (.out(button_2_out));
  or or_1 (or_1_out, TN, button_1_out);
  or or_2 (or_2_out, TE, button_1_out);
  or or_3 (or_3_out, WW, button_2_out);
  or or_4 (or_4_out, WE, button_2_out);
  Button Traffic_Jam_Sensor__N (.out(TN));
  LED led_1 (.in(TN));
  Button Walker__W (.out(WW));
  Clock CLOCK (.out(C1));
  LED R (.in(U1_n_left[1]));
  LED L (.in(U1_n_left[0]));
  LED L_2 (.in(U1_w_left[0]));
  LED G (.in(U1_w_left[1]));
  LED R_2 (.in(U1_w_left[2]));
  FreqDivider U2 (.CLOCK(C1), .CLK(C2));
  WalkerModifier U3 (
    .WWm(U3_wwm), .WW(or_3_out), .WEm(U3_wem), .WE(or_4_out), .CLK(C1), .RS_W(U1_rs_w), .RS_E(U1_rs_e));
  LED G_2 (.in(U1_e_green[0]));
  LED R_3 (.in(U1_e_green[1]));
  LED led_2 (.in(TE));
  Button Traffic_Jam_Sensor__E (.out(TE));
  Button Walker__E (.out(WE));
  Controller U1 (
    .CLK(C2), .TN(or_1_out), .TE(or_2_out), .NIGHT(NIGHT), .WWm(U3_wwm), .WEm(U3_wem),
    .W_Green(U1_w_left[1]), .W_Red(U1_w_left[2]), .N_Left(U1_n_left[0]), .N_Red(U1_n_left[1]),
    .E_Green(U1_e_green[0]), .E_Red(U1_e_green[1]), .W_Left(U1_w_left[0]), .RS_W(U1_rs_w), .RS_E(U1_rs_e));
  Hex_Digit_Display hex_digit_display_1 (.value(grading_1_out_4));  // open: dp
  Grading grading_1 (.Light({U1_e_green, U1_n_left, U1_w_left}), .CLK(C2), .CLOCK(C1), .out_4(grading_1_out_4));

  // Notes on the sheet:
  //   2016312761 여혁수
  //   Copyright (c) 2015-2019 by Hyonug Bok Min, All rights reserved.
  //   W
  //   N
  //   CLK
  //   HW0 version 2.0
  //   Traffic Light Controller
  //   E
  //   (Choose 64 Hz for operation)
  //   채점 회로 
  //   3
  //   0
  //   2
  //   3
endmodule

module Controller (
  input  CLK,
  input  TN,
  input  TE,
  input  NIGHT,
  input  WWm,
  input  WEm,
  output W_Left,
  output W_Green,
  output W_Red,
  output N_Left,
  output N_Red,
  output E_Green,
  output E_Red,
  output RS_W,
  output RS_E
);

  wire mycontroller_1_ns0, mycontroller_1_ns1, mycontroller_1_ns2;

  MyController mycontroller_1 (
    .CLK(CLK), .TN(TN), .TE(TE), .NIGHT(NIGHT), .WW(WWm), .WE(WEm), .NS2(mycontroller_1_ns2),
    .NS1(mycontroller_1_ns1), .NS0(mycontroller_1_ns0));
  Signaller signaller_1 (
    .NS2(mycontroller_1_ns2), .NS1(mycontroller_1_ns1), .NS0(mycontroller_1_ns0), .W_Red(W_Red),
    .W_Green(W_Green), .W_Left(W_Left), .N_Red(N_Red), .N_Left(N_Left), .E_Green(E_Green), .E_Red(E_Red),
    .RS_W(RS_W), .RS_E(RS_E));
  // TrafficLight trafficlight_1: pin names not known

  // Notes on the sheet:
  //   Controller - State Machine
endmodule

// FD
module FreqDivider (
  input  CLOCK,
  output CLK
);

  MyFreqDivider myfreqdivider_1 (.CLOCK(CLOCK), .CLK(CLK));
  // ice3024n_FreqDivider freqdivider_1: pin names not known

  // Notes on the sheet:
  //   Frequency Divider
endmodule

// Walker
module WalkerModifier (
  input  CLK,
  input  WW,
  input  RS_W,
  input  WE,
  input  RS_E,
  output WWm,
  output WEm
);

  wire d_ff_1_q, d_ff_2_q;

  D_Flip_Flop d_ff_1 (.clk(CLK), .D(RS_W), .Q(d_ff_1_q));  // open: Qn, preset, en, reset
  D_Flip_Flop d_ff_2 (.clk(CLK), .D(RS_E), .Q(d_ff_2_q));  // open: Qn, preset, en, reset
  D_Flip_Flop d_ff_3 (.clk(1'b0), .Q(WWm), .preset(WW), .reset(d_ff_1_q));  // open: D, Qn, en
  D_Flip_Flop d_ff_4 (.clk(1'b0), .Q(WEm), .preset(WE), .reset(d_ff_2_q));  // open: D, Qn, en

  // Notes on the sheet:
  //   Copyright (c) 2015 by Hyonug Bok Min, All rights reserved.
  //   WARNING : THIS IS SIMPLY AN EXAMPLE
  //   Walker Signal Modifier
  //   NOTE : The following 2 Fliplops are actually RS-latches
  //   YOU MAY MODIFY THIS CIRCUIT IF YOU NEED
  //   NOTE : The above 2 Fliplops are used to remove hazards, i.e., glitches.
endmodule

module Grading (
  input  [6:0] Light,
  input  CLK,
  input  CLOCK,
  output [3:0] out_4
);

  wire comparator_1_lt, comparator_2_gt, comparator_3_eq, comparator_4_eq, comparator_5_eq, comparator_6_eq,
       d_ff_1_q, d_ff_2_qn, d_ff_3_q, d_ff_4_q, d_ff_5_q, d_ff_6_q, nand_1_out, not_1_out, not_2_out;
  wire [1:0] priority_encoder_1_out;
  wire [3:0] and_1_out;
  wire [7:0] counter_1_q;

  D_Flip_Flop d_ff_1 (.clk(CLOCK), .D(CLK), .Q(d_ff_1_q));  // open: Qn, preset, en, reset
  Counter #(.ongoal("stay")) counter_1 (.Q(counter_1_q), .clk(CLOCK), .clr(not_1_out));  // open: load, D, count, carry
  not not_1 (not_1_out, CLK);
  D_Flip_Flop d_ff_2 (.clk(CLK), .D(1'b1), .Qn(d_ff_2_qn));  // open: Q, preset, en, reset
  Comparator comparator_1 (.a(counter_1_q), .b(8'h8), .lt(comparator_1_lt));  // open: gt, eq
  Comparator comparator_2 (.a(counter_1_q), .b(8'h1), .gt(comparator_2_gt));  // open: eq, lt
  Comparator #(.width(7)) comparator_3 (.a(7'b0110010), .b(Light), .eq(comparator_3_eq));  // open: gt, lt
  Comparator #(.width(7)) comparator_4 (.a(7'b1010011), .b(Light), .eq(comparator_4_eq));  // open: gt, lt
  Comparator #(.width(7)) comparator_5 (.a(7'b1010001), .b(Light), .eq(comparator_5_eq));  // open: gt, lt
  Comparator #(.width(7)) comparator_6 (.a(7'b1001100), .b(Light), .eq(comparator_6_eq));  // open: gt, lt
  D_Flip_Flop d_ff_3 (.clk(d_ff_1_q), .D(comparator_3_eq), .Q(d_ff_3_q), .preset(d_ff_2_qn));  // open: Qn, en, reset
  D_Flip_Flop d_ff_4 (.clk(d_ff_1_q), .D(comparator_4_eq), .Q(d_ff_4_q));  // open: Qn, preset, en, reset
  D_Flip_Flop d_ff_5 (.clk(d_ff_1_q), .D(comparator_5_eq), .Q(d_ff_5_q));  // open: Qn, preset, en, reset
  D_Flip_Flop d_ff_6 (.clk(d_ff_1_q), .D(comparator_6_eq), .Q(d_ff_6_q));  // open: Qn, preset, en, reset
  nand nand_1 (nand_1_out, comparator_1_lt, comparator_2_gt);
  Priority_Encoder #(.select(2)) priority_encoder_1 (
    .in0(d_ff_3_q), .in1(d_ff_4_q), .in2(d_ff_5_q), .in3(d_ff_6_q), .out(priority_encoder_1_out), .en_in(1'b1));  // open: gs, en_out
  nor nor_1 (and_1_out[3], d_ff_3_q, d_ff_6_q, d_ff_5_q, d_ff_4_q);
  not not_2 (not_2_out, and_1_out[3]);
  and and_1 (and_1_out[0], not_2_out, priority_encoder_1_out[0]);
  or or_1 (and_1_out[1], priority_encoder_1_out[1], and_1_out[3]);
  assign out_4 = nand_1_out ? {{2{and_1_out[3]}}, and_1_out[1:0]} : 4'bz;  // Controlled_Buffer controlled_buffer_1

  // Notes on the sheet:
  //   Copyright (c) by Hyoung Bok Min, All rights reserved.
  //   This is Grading Purpose Only
  //   invalid state
endmodule

module MyFreqDivider (
  input  CLOCK,
  output CLK
);

  wire d_ff_1_q, d_ff_1_qn, d_ff_2_q, d_ff_2_qn, d_ff_3_q, d_ff_3_qn, d_ff_4_q, d_ff_4_qn, d_ff_5_q,
       d_ff_5_qn;
  wire [7:0] counter_1_q;

  D_Flip_Flop d_ff_1 (.clk(CLOCK), .D(d_ff_1_qn), .Q(d_ff_1_q), .Qn(d_ff_1_qn));  // open: preset, en, reset
  D_Flip_Flop d_ff_2 (.clk(d_ff_1_q), .D(d_ff_2_qn), .Q(d_ff_2_q), .Qn(d_ff_2_qn));  // open: preset, en, reset
  D_Flip_Flop d_ff_3 (.clk(d_ff_2_q), .D(d_ff_3_qn), .Q(d_ff_3_q), .Qn(d_ff_3_qn));  // open: preset, en, reset
  D_Flip_Flop d_ff_4 (.clk(d_ff_3_q), .D(d_ff_4_qn), .Q(d_ff_4_q), .Qn(d_ff_4_qn));  // open: preset, en, reset
  D_Flip_Flop d_ff_5 (.clk(d_ff_4_q), .D(d_ff_5_qn), .Q(d_ff_5_q), .Qn(d_ff_5_qn));  // open: preset, en, reset
  Counter counter_1 (
    .Q({counter_1_q[7:3], CLK, counter_1_q[1:0]}), .clk(d_ff_5_q));  // open: load, D, count, carry, clr
endmodule

module Signaller (
  input  NS2,
  input  NS1,
  input  NS0,
  output W_Red,
  output W_Green,
  output W_Left,
  output N_Red,
  output N_Left,
  output E_Green,
  output E_Red,
  output RS_W,
  output RS_E
);

  wire U12_out, U13_out, U14_out, U15_out, U16_out, U17_out, U19_out, U21_out, U22_out, U23_out;

  not U12 (U12_out, NS2);
  not U14 (U14_out, NS1);
  not U21 (U21_out, NS0);
  nor U27 (E_Green, NS0, NS1);
  nand U13 (U13_out, NS1, U12_out);
  nand U15 (U15_out, NS2, U14_out);
  nand U22 (U22_out, U21_out, U14_out);
  nor U30 (RS_E, NS0, U14_out, NS2);
  nand U16 (U16_out, U13_out, U15_out);
  nand U17 (U17_out, NS0, U16_out);
  not U18 (W_Red, U17_out);
  nand U19 (U19_out, U17_out, U14_out);
  nand U23 (U23_out, U17_out, U22_out, U12_out);
  not U26 (N_Left, U17_out);
  not U29 (RS_W, U17_out);
  not U20 (W_Green, U19_out);
  not U24 (W_Left, U23_out);
  nand U25 (N_Red, U23_out, U19_out);
  nand U28 (E_Red, U17_out, U23_out);

  // Notes on the sheet:
  //   signaller.txt  by 'pla2circ signaller.txt' (pla2circ v0.21)
endmodule

module MyController (
  input  CLK,
  input  TN,
  input  TE,
  input  NIGHT,
  input  WW,
  input  WE,
  output NS2,
  output NS1,
  output NS0
);

  wire U11_out, U12_out, U13_out, U14_out, U15_out, U16_out, U17_out, U18_out, U19_out, U20_out, U21_out,
       U22_out, U23_out, U24_out, U25_out, U26_out, U27_out, U28_out, U29_out, U30_out, U31_out, U32_out,
       U33_out, U34_out, U35_out, U36_out, U37_out, U38_out, U39_out, U40_out;

  nand U11 (U11_out, TN, NS0, NS1);
  not U12 (U12_out, NS0);
  not U13 (U13_out, NS1);
  not U16 (U16_out, TN);
  not U19 (U19_out, NIGHT);
  not U20 (U20_out, NS2);
  nand U24 (U24_out, WW, NIGHT);
  nand U28 (U28_out, NS0, NS1);
  nand U14 (U14_out, U12_out, U13_out);
  nand U23 (U23_out, NS1, U19_out);
  nand U27 (U27_out, U19_out, NS0, U13_out);
  nand U37 (U37_out, TE, U20_out);
  not U15 (U15_out, U14_out);
  nand U25 (U25_out, U23_out, U24_out);
  nand U29 (U29_out, U28_out, U14_out);
  not U38 (U38_out, U14_out);
  nand U17 (U17_out, U15_out, TE, U16_out);
  nand U26 (U26_out, U25_out, U12_out);
  nand U30 (U30_out, U29_out, WE, NIGHT);
  nand U36 (U36_out, U25_out, U12_out, U20_out);
  nand U39 (U39_out, U37_out, U38_out, U19_out);
  nand U18 (U18_out, U11_out, U17_out);
  nand U31 (U31_out, U26_out, U27_out, U30_out);
  nand U21 (U21_out, U18_out, U19_out, U20_out);
  not U32 (U32_out, U31_out);
  not U22 (U22_out, U21_out);
  nor U33 (U33_out, U32_out, NS2);
  not U34 (U34_out, U21_out);
  nand U35 (U35_out, U34_out, TN);
  nand U40 (U40_out, U35_out, U36_out, U39_out);
  D_Flip_Flop d_ff_1 (.clk(CLK), .D(U22_out), .Q(NS2));  // open: Qn, preset, en, reset
  D_Flip_Flop d_ff_2 (.clk(CLK), .D(U33_out), .Q(NS1));  // open: Qn, preset, en, reset
  D_Flip_Flop d_ff_3 (.clk(CLK), .D(U40_out), .Q(NS0));  // open: Qn, preset, en, reset

  // Notes on the sheet:
  //   controller.txt  by 'pla2circ controller.txt' (pla2circ v0.21)
endmodule
