// Logisim project signaller.circ as structural Verilog: 1 circuit, main circuit main
// pla2circ
module main (
  input  NS2,
  input  NS1,
  input  NS0,
  output W_Red,
  output W_Green,
  output W_Left,
  output N_Red,
  output N_Left,
  output E_Green,
  output E_Red,
  output RS_W,
  output RS_E
);

  wire U12_out, U13_out, U14_out, U15_out, U16_out, U17_out, U19_out, U21_out, U22_out, U23_out, undriven,
       undriven_2, undriven_3, undriven_4, undriven_5, undriven_6, undriven_7, undriven_8, undriven_9,
       undriven_10, undriven_11, undriven_12, undriven_13, undriven_14, undriven_15;

  not U12 (U12_out, NS2);
  not U14 (U14_out, NS1);
  not U21 (U21_out, NS0);
  nor U27 (E_Green, undriven, NS1);
  nand U13 (U13_out, NS1, undriven_5);
  nand U15 (U15_out, undriven_3, undriven_6);
  nand U22 (U22_out, U21_out, undriven_4);
  nor U30 (RS_E, NS0, U14_out, undriven_2);
  nand U16 (U16_out, U13_out, U15_out);
  nand U17 (U17_out, NS0, U16_out);
  not U18 (W_Red, U17_out);
  nand U19 (U19_out, undriven_9, undriven_7);
  nand U23 (U23_out, undriven_10, U22_out, U12_out);
  not U26 (N_Left, undriven_11);
  not U29 (RS_W, undriven_8);
  not U20 (W_Green, U19_out);
  not U24 (W_Left, U23_out);
  nand U25 (N_Red, undriven_14, undriven_15);
  nand U28 (E_Red, undriven_12, undriven_13);

  // Notes on the sheet:
  //   signaller.txt  by 'pla2circ signaller.txt' (pla2circ v0.21)
endmodule
